# Fritzing sketch Untitled Sketch (saved by Fritzing 0.9.0b)
breadboards: 1

parts:
  M1 = DC Motor
  M2 = DC Motor
  IC1 = L293D [package=THT]
  IR1 = TSOP312.., 314.. [package=THT]
  Parte1 = Arduino Uno (Rev3)

nets:
  N1: M1.pin_1, IC1.Out_2_(_Controlled_by_Enable_1_)
  N2: M1.pin_2, IC1.Out_1_(_Controlled_by_Enable_1_)
  N3: M2.pin_1, IC1.Out_4_(_Controlled_by_Enable_2_)
  N4: M2.pin_2, IC1.Out_3_(_Controlled_by_Enable_2_)
  N5: IC1.In_1, Parte1.D10_PWM/SS
  GND: IC1.0V, IR1.GND, Parte1.GND
  N6: IC1.In_2, Parte1.D12/MISO
  N7: IC1.+Vmotor, IC1.+V, IR1.Vs, Parte1.5V
  N8: IC1.In_3, Parte1.D8
  N9: IC1.In_4, Parte1.D6_PWM
  N10: IR1.Data, Parte1.D4
